# Fritzing sketch breadboard-looloog-proto (saved by Fritzing 1.0.6)
breadboards: 2

parts:
  R1 = Resistor [tolerance=±5% power=0.25W resistance=10k package=THT]
  Part1 = 74HC4067
  Pro_Micro1 = SparkFun Pro Micro
  S1 = Pushbutton [package="[THT]"]
  R2 = Rotary Potentiometer (Large) [maximum_resistance=100kΩ knob_status=50% power=0.5W package=THT]
  R3 = Rotary Potentiometer (Large) [maximum_resistance=100kΩ knob_status=50% power=0.5W package=THT]
  Part2 = 74HC4067
  LED1 = smd LED [color="Red (633nm)" package="0603 [SMD]"]
  R4 = Resistor [tolerance=±5% power=0.25W resistance=10k package=THT]

nets:
  VCC: R1.Pin_0, Part1.VCC, Pro_Micro1.VCC, R2.leg1, R3.leg1, Part2.VCC, R4.Pin_0
  N1: R1.Pin_1, S1.Pin_3, S1.Pin_4, Part2.I15
  N2: Part1.COMMON_I/O, Pro_Micro1.A3
  N3: Part1.S0, Pro_Micro1.2, Part2.S0
  N4: Part1.S1, Pro_Micro1.3, Part2.S1
  GND: Part1.GND, Pro_Micro1.RAW, S1.Pin_1, S1.Pin_2, R2.leg2, R3.leg2, Part2.GND, LED1.anode
  N5: Part1.S3, Pro_Micro1.5, Part2.S3
  N6: Part1.S2, Pro_Micro1.4, Part2.S2
  N7: Part1.E, Pro_Micro1.6
  N8: Part1.I15, R2.wiper
  N9: Pro_Micro1.7, Part2.E
  N10: Pro_Micro1.A2, Part2.COMMON_I/O
  N11: R3.wiper, Part2.I7
  N12: LED1.cathode, R4.Pin_1

custom parts:
  74HC4067: 16-Channel Analog Multiplexer and Demultiplexer
  SparkFun Pro Micro: The Pro Micro is similar to the Pro Mini except with an ATmega32U4 on board. The USB transceiver inside the 32U4 allows us to add USB connectivity on-board and do away with bulky external USB interface. Based on: https://github.com/unorthodox-engineers/unorthodox-arduino/blob/master/Unorthodox/fritzing/parts/Pro%20Micro.fzpz
